# Fritzing sketch circuit_diagram (saved by Fritzing 1.0.3)
breadboards: 1

parts:
  ESP32-WROOM = ESP32-38PinWide
  VS1053 = Adafruit VS1053 Codec + MicroSD Breakout - MP3/WAV/MIDI/OGG
  TFT_ST7735 = TFT 1.8 inch 160x128 w microSD
  Encoder = Rotary Encoder [package=THT]
  Enc_SW = SWITCH-MOMENTARY-2 [package=tactile-pth-12mm]

nets:
  3.3V: ESP32-WROOM.3.3, VS1053.3.3V, VS1053.RST_5V, TFT_ST7735.RESET, TFT_ST7735.+5V
  N1: ESP32-WROOM.GPIO32, VS1053.XDCS_5V
  N2: ESP32-WROOM.GPIO33, TFT_ST7735.LITE
  N3: ESP32-WROOM.GPIO25, Encoder.EncoderPinA
  N4: ESP32-WROOM.GPIO26, Encoder.EncoderPinB
  N5: ESP32-WROOM.GPIO27, Enc_SW.1
  GND: ESP32-WROOM.GND, VS1053.GND, TFT_ST7735.GND, Encoder.EncoderPinC, Enc_SW.2
  N6: ESP32-WROOM.GPIO15, TFT_ST7735.TFTCS
  N7: ESP32-WROOM.GPIO2, TFT_ST7735.TFTDC
  N8: ESP32-WROOM.GPIO4, VS1053.DREQ
  N9: ESP32-WROOM.GPIO5, VS1053.CS_5V
  N10: ESP32-WROOM.GPIO18, VS1053.SCLK_5V, TFT_ST7735.SCLK
  N11: ESP32-WROOM.GPIO19, VS1053.MISO, TFT_ST7735.MISO
  N12: ESP32-WROOM.GPIO21, VS1053.SDCS_5V
  N13: ESP32-WROOM.GPIO23, VS1053.MOSI_5V, TFT_ST7735.MOSI

custom parts:
  ESP32-38PinWide: Generic 38-Pin ESP32 with wide format (only access to one side of pins on a breadboard) based on Stephen Lilley's HiLetgo ESP-WROOM-32 ESP32 ESP-32S Development Board.
  Adafruit VS1053 Codec + MicroSD Breakout - MP3/WAV/MIDI/OGG: This breakout board is the ultimate companion for the VLSI VS1053B DSP codec chip. The VS1053 can decode a wide variety of audio formats such as MP3, AAC, Ogg Vorbis, WMA, MIDI, FLAC, WAV (PCM and ADPCM). It can also be used to record audio in both PCM (WAV) and compressed Ogg Vorbis. You can do all sorts of stuff with the audio as well such as adjusting bass, treble, and volume digitally.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
  TFT 1.8 inch 160x128 w microSD: This lovely little display breakout is the best way to add a small, colorful and bright display to any project. Since the display uses 4-wire SPI to communicate and has its own pixel-addressable frame buffer, it can be used with every kind of microcontroller. Even a very small one with low memory and few pins available! The 1.8" display has 128x160 color pixels.
