# Fritzing sketch circuit_diagram_cam_headless (saved by Fritzing 1.0.3)
breadboards: 1

parts:
  ESP32-CAM = ESP32-CAM AI-Thinker (no camera)
  VS1053 = Adafruit VS1053 Codec + MicroSD Breakout - MP3/WAV/MIDI/OGG
  Encoder = Rotary Encoder [package=THT]
  Enc_SW = SWITCH-MOMENTARY-2 [package=tactile-pth-12mm]

nets:
  3V3: ESP32-CAM.3V3, VS1053.3.3V, VS1053.RST_5V
  GND: ESP32-CAM.GND, VS1053.GND, Encoder.EncoderPinC, Enc_SW.2
  N1: ESP32-CAM.GPIO4, VS1053.DREQ
  N2: ESP32-CAM.GPIO5, VS1053.CS_5V
  N3: ESP32-CAM.GPIO18, VS1053.SCLK_5V
  N4: ESP32-CAM.GPIO19, VS1053.MISO
  N5: ESP32-CAM.GPIO23, VS1053.MOSI_5V
  N6: ESP32-CAM.GPIO25, Encoder.EncoderPinA
  N7: ESP32-CAM.GPIO26, Encoder.EncoderPinB
  N8: ESP32-CAM.GPIO27, Enc_SW.1
  N9: ESP32-CAM.GPIO32, VS1053.XDCS_5V

custom parts:
  ESP32-CAM AI-Thinker (no camera): Minimal ESP32-CAM (AI-Thinker) wiring part for headless Webradio use. Includes 3V3, GND and GPIOs used by VS1053, SPI and rotary encoder. SD_MMC pins GPIO2 (D0), GPIO14 (CLK), GPIO15 (CMD) are labeled as onboard only. Some GPIOs are camera FPC pads when the camera is fitted; use without camera.
  Adafruit VS1053 Codec + MicroSD Breakout - MP3/WAV/MIDI/OGG: This breakout board is the ultimate companion for the VLSI VS1053B DSP codec chip. The VS1053 can decode a wide variety of audio formats such as MP3, AAC, Ogg Vorbis, WMA, MIDI, FLAC, WAV (PCM and ADPCM). It can also be used to record audio in both PCM (WAV) and compressed Ogg Vorbis. You can do all sorts of stuff with the audio as well such as adjusting bass, treble, and volume digitally.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
